// Logisim project Guia_0801.circ as structural Verilog: 1 circuit, main circuit main
module main (
  input  in_1,
  input  in_2,
  input  in_3,
  input  in_4,
  input  in_5,
  input  in_6,
  input  in_7,
  input  in_8,
  input  in_9,
  input  in_10,
  input  in_11,
  output out_12,
  output out_13,
  output out_14,
  output out_15,
  output out_16
);

  wire full_adder_1_p6, full_adder_2_p5, full_adder_3_p5, full_adder_4_p5;

  // full_adder full_adder_1: pin names not known; wires that end beside it: in_1, in_2, in_3, in_1, out_12, full_adder_1_p6
  // full_adder full_adder_2: pin names not known; wires that end beside it: in_4, in_5, full_adder_1_p6, out_13, full_adder_2_p5
  // full_adder full_adder_3: pin names not known; wires that end beside it: in_6, in_7, full_adder_2_p5, out_14, full_adder_3_p5
  // full_adder full_adder_4: pin names not known; wires that end beside it: in_8, in_9, full_adder_3_p5, out_15, full_adder_4_p5
  // full_adder full_adder_5: pin names not known; wires that end beside it: in_10, in_11, full_adder_4_p5, out_16, 1'b0

  // Notes on the sheet:
  //   Não sei se está correto. Começo$escrevendo pelo bit menos significado$(little endian) e a resposta é dada do $mesmo modo.
endmodule
