// Logisim project Guia_0804.circ as structural Verilog: 1 circuit, main circuit main
module main (
  input  in_1,
  input  in_2,
  input  in_3,
  input  in_4,
  input  in_5,
  input  in_6,
  input  in_7,
  input  in_8,
  input  in_9,
  input  in_10,
  output out_11
);

  wire main_1_p3, main_2_p3, main_3_p3, main_4_p3, main_5_p3, or_1_out, or_2_out;

  // unequal_main main_1: pin names not known; wires that end beside it: in_1, in_2, main_1_p3
  // unequal_main main_2: pin names not known; wires that end beside it: in_3, in_4, main_2_p3
  // unequal_main main_3: pin names not known; wires that end beside it: in_5, in_6, main_3_p3
  // unequal_main main_4: pin names not known; wires that end beside it: in_7, in_8, main_4_p3
  // unequal_main main_5: pin names not known; wires that end beside it: in_9, in_10, main_5_p3
  or or_1 (or_1_out, main_1_p3, main_2_p3, main_3_p3);
  or or_2 (or_2_out, main_4_p3, main_5_p3);
  or or_3 (out_11, or_1_out, or_2_out);
endmodule
