// Logisim project Guia_0805.circ as structural Verilog: 1 circuit, main circuit main
module main (
  input  in_1,
  input  in_2,
  input  in_3,
  input  in_4,
  input  in_5,
  input  in_6,
  input  in_7,
  output out_8,
  output out_9,
  output out_10,
  output out_11,
  output out_12
);

  wire full_adder_1_p3, full_adder_2_p5, full_adder_3_p5, full_adder_4_p5, full_adder_5_p10, not_1_out,
       not_2_out, not_3_out, not_4_out, not_6_out;

  not not_1 (not_1_out, in_2);
  not not_2 (not_2_out, in_4);
  not not_3 (not_3_out, in_3);
  not not_4 (not_4_out, in_5);
  not not_5 (not_1_out, in_7);
  not not_6 (not_6_out, in_6);
  // full_adder full_adder_1: pin names not known; wires that end beside it: in_1, out_8, full_adder_1_p3
  // full_adder full_adder_2: pin names not known; wires that end beside it: not_3_out, in_7, full_adder_1_p3, out_9, full_adder_2_p5
  // full_adder full_adder_3: pin names not known; wires that end beside it: not_2_out, in_7, full_adder_2_p5, out_10, full_adder_3_p5
  // full_adder full_adder_4: pin names not known; wires that end beside it: not_4_out, in_7, full_adder_3_p5, out_11, full_adder_4_p5
  // full_adder full_adder_5: pin names not known; wires that end beside it: in_5, not_4_out, in_6, not_6_out, not_6_out, in_7, full_adder_4_p5, in_7, out_12, full_adder_5_p10, full_adder_5_p10
endmodule
