// Logisim project Recuperacao_01020B.circ as structural Verilog: 1 circuit, main circuit main
module main (
  input  a,
  input  b,
  input  c,
  output out_4
);

  wire and_1_out, and_2_out, and_3_out, and_4_out, and_5_out, and_6_out, not_1_out, not_2_out, not_3_out,
       not_4_out, not_5_out, not_6_out, or_1_out, or_2_out;

  not not_1 (not_1_out, b);
  and and_1 (and_1_out, not_1_out, a);
  and and_2 (and_2_out, b, not_2_out);
  not not_2 (not_2_out, a);
  not not_3 (not_3_out, b);
  and and_3 (and_3_out, not_3_out, a);
  and and_4 (and_4_out, b, not_4_out);
  not not_4 (not_4_out, a);
  not not_5 (not_5_out, or_1_out);
  or or_1 (or_1_out, and_1_out, and_2_out);
  or or_2 (or_2_out, and_3_out, and_4_out);
  not not_6 (not_6_out, c);
  and and_5 (and_5_out, not_5_out, c);
  or or_3 (out_4, and_5_out, and_6_out);
  and and_6 (and_6_out, or_2_out, not_6_out);
endmodule
