// Logisim project Recuperacao_0103A.circ as structural Verilog: 1 circuit, main circuit main
module main (
  input  a,
  input  b,
  input  c,
  output out_4
);

  wire not_1_out, not_2_out, or_1_out, or_2_out;

  not not_1 (not_1_out, a);
  or or_1 (or_1_out, not_1_out, b);
  or or_2 (or_2_out, b, not_2_out);
  not not_2 (not_2_out, c);
  and and_1 (out_4, or_1_out, or_2_out);
endmodule
